// Logisim project 1805006.circ as structural Verilog: 1 circuit, main circuit main
module main (
  input  X1,
  input  X2,
  output Z1,
  output Z2,
  output Q1,
  output Q2
);

  wire clock_1_out, n7404_1_p2, n7404_1_p4, n7408_1_p1, n7408_1_p5, n7408_1_p6, n7408_1_p8, n7408_1_p11,
       n7408_2_p3, n7408_2_p6, n7408_2_p9, n7408_2_p12, n7408_3_p6, n7408_3_p9, n7408_3_p12, n7408_4_p3,
       n7408_5_p12, n7408_6_p6, n7432_1_p3, n7432_1_p6, n7432_1_p8, n7432_1_p9, n7432_1_p10, n7432_1_p11,
       n7432_1_p12, n7432_2_p2, n7432_2_p3, n7432_2_p5, n7432_2_p7, n7432_2_p8, n7432_2_p9, n7432_2_p11,
       n7432_2_p12, n7474_1_p5, n7474_1_p8;

  // _7404 7404_1: pin names not known; wires that end beside it: X1, n7404_1_p2, X2, n7404_1_p4
  // _7408 7408_1: pin names not known; wires that end beside it: n7408_1_p1, n7408_1_p1, n7404_1_p2, X2, n7408_1_p5, n7408_1_p6, n7408_1_p5, n7408_1_p8, n7408_1_p6, n7404_1_p2, n7408_1_p11
  Clock clock_1 (.out(clock_1_out));
  // _7408 7408_2: pin names not known; wires that end beside it: n7408_1_p11, Q2, n7408_2_p3, X1, n7404_1_p4, n7408_2_p6, n7408_2_p6, Q1, n7408_2_p9, n7404_1_p4, Q1, n7408_2_p12
  // _7432 7432_1: pin names not known; wires that end beside it: n7408_1_p8, n7408_2_p3, n7432_1_p3, n7432_1_p3, n7408_2_p9, n7432_1_p6, n7432_1_p6, n7432_1_p8, n7432_1_p9, n7432_1_p10, n7432_1_p11, n7432_1_p12
  // _7474 7474_1: pin names not known; wires that end beside it: n7432_1_p9, clock_1_out, Q1, n7408_1_p6, n7474_1_p5, clock_1_out, Q2, n7474_1_p8
  // _7408 7408_3: pin names not known; wires that end beside it: n7408_2_p12, n7474_1_p8, n7432_1_p8, n7404_1_p4, n7404_1_p2, n7408_3_p6, n7408_3_p6, n7474_1_p8, n7408_3_p9, n7404_1_p2, X2, n7408_3_p12
  // _7432 7432_2: pin names not known; wires that end beside it: n7408_3_p9, n7432_2_p2, n7432_2_p3, n7432_2_p3, n7432_2_p5, n7474_1_p5, n7432_2_p7, n7432_2_p8, n7432_2_p9, n7432_2_p9, n7432_2_p11, n7432_2_p12
  // _7408 7408_4: pin names not known; wires that end beside it: X1, X2, n7408_4_p3, n7408_4_p3, Q2, n7432_1_p10, n7408_4_p3, Q1, n7432_1_p11
  // _7408 7408_5: pin names not known; wires that end beside it: n7408_3_p12, Q2, n7432_2_p2, X1, n7404_1_p4, n7432_2_p7, n7432_2_p7, Q2, n7432_2_p5, n7404_1_p2, Q1, n7408_5_p12
  // _7408 7408_6: pin names not known; wires that end beside it: n7408_5_p12, Q2, n7432_2_p8, n7404_1_p2, X2, n7408_6_p6, n7408_6_p6, Q1, n7432_2_p11
  // _7474 7474_2: pin names not known; wires that end beside it: n7432_2_p12, clock_1_out, Z1, n7432_1_p12, clock_1_out, Z2
endmodule
