// Logisim project MJKFinal.circ as structural Verilog
module main (
  input  C,
  input  J,
  input  K,
  output Q,
  output Q_prime
);

  wire n7400_1_p3, n7400_1_p4, n7400_1_p6, n7400_1_p11, n7400_1_p12, n7400_1_p14, n7400_3_p2, n7400_3_p3,
       n7400_3_p10, n7400_3_p13, n7400_4_p3;

  // _7400 7400_1: pin names not known; wires that end beside it: Q_prime, C, n7400_1_p3, n7400_1_p4, J, n7400_1_p6, 1'b0, 1'b1, C, Q, n7400_1_p11, n7400_1_p12, K, n7400_1_p14
  // _7400 7400_2: pin names not known; wires that end beside it: n7400_1_p3, n7400_1_p3, n7400_1_p4, 1'b0, 1'b1, n7400_1_p12, 1'b0
  // _7400 7400_3: pin names not known; wires that end beside it: n7400_1_p6, n7400_3_p2, n7400_3_p3, n7400_3_p3, n7400_1_p14, n7400_3_p2, 1'b1, C, C, n7400_3_p10, n7400_3_p3, n7400_3_p10, n7400_3_p13
  // _7400 7400_4: pin names not known; wires that end beside it: n7400_3_p10, n7400_3_p2, n7400_4_p3, n7400_4_p3, Q, Q_prime, 1'b0, 1'b1, n7400_3_p13, Q_prime, Q
endmodule

module register (
  input  right_serial,
  input  A,
  input  B,
  input  C,
  input  D,
  input  left_serial,
  input  S0,
  input  S1,
  input  in_9,
  output out_10,
  output out_11,
  output out_12,
  output out_13
);

  wire and_1_out, and_2_out, and_3_out, and_4_out, and_5_out, and_6_out, and_7_out, and_8_out, and_9_out,
       and_10_out, and_11_out, and_12_out, and_13_out, Clock_out, nor_1_out, nor_2_out, nor_3_out, nor_4_out,
       nor_5_out, nor_6_out, not_1_out, not_2_out, not_3_out, not_4_out, not_5_out, not_6_out, not_7_out,
       not_8_out;

  not not_1 (not_1_out, S0);
  not not_2 (not_2_out, S1);
  Clock Clock (.out(Clock_out));
  nor nor_1 (nor_1_out, not_1_out, not_2_out);
  and and_1 (and_1_out, not_2_out, not_1_out);
  not not_3 (not_3_out, Clock_out);
  not not_4 (not_4_out, in_9);
  and and_2 (and_2_out, right_serial, not_2_out);
  nor nor_2 (nor_2_out, and_1_out, not_3_out);
  and and_3 (and_3_out, nor_1_out, A);
  nor nor_3 (nor_3_out, and_2_out, and_3_out, and_4_out);
  and and_4 (and_4_out, not_1_out, out_11);
  not not_5 (not_5_out, nor_3_out);
  and and_5 (and_5_out, nor_1_out, B);
  and and_6 (and_6_out, out_10, not_2_out);
  S_R_Flip_Flop s_r_ff_1 (
    .S(not_5_out), .clk(nor_2_out), .R(nor_3_out), .Q(out_10), .reset(not_4_out));  // open: Qn, preset, en
  and and_7 (and_7_out, not_1_out, out_12);
  nor nor_4 (nor_4_out, and_6_out, and_5_out, and_7_out);
  and and_8 (and_8_out, out_11, not_2_out);
  not not_6 (not_6_out, nor_4_out);
  and and_9 (and_9_out, nor_1_out, C);
  nor nor_5 (nor_5_out, and_8_out, and_9_out, and_10_out);
  S_R_Flip_Flop s_r_ff_2 (
    .S(not_6_out), .clk(nor_2_out), .R(nor_4_out), .Q(out_11), .reset(not_4_out));  // open: Qn, preset, en
  and and_10 (and_10_out, not_1_out, out_13);
  not not_7 (not_7_out, nor_5_out);
  and and_11 (and_11_out, nor_1_out, D);
  and and_12 (and_12_out, out_12, not_2_out);
  nor nor_6 (nor_6_out, and_12_out, and_11_out, and_13_out);
  S_R_Flip_Flop s_r_ff_3 (
    .S(not_7_out), .clk(nor_2_out), .R(nor_5_out), .Q(out_12), .reset(not_4_out));  // open: Qn, preset, en
  and and_13 (and_13_out, not_1_out, left_serial);
  not not_8 (not_8_out, nor_6_out);
  S_R_Flip_Flop s_r_ff_4 (
    .S(not_8_out), .clk(nor_2_out), .R(nor_6_out), .Q(out_13), .reset(not_4_out));  // open: Qn, preset, en
endmodule

module registerD (
  input  right_serial,
  input  A,
  input  B,
  input  C,
  input  D,
  input  left_serial,
  input  S0,
  input  S1,
  input  clear,
  output QA,
  output QB,
  output QC,
  output QD
);

  wire and_1_out, and_2_out, and_3_out, and_4_out, and_5_out, and_6_out, and_7_out, and_8_out, and_9_out,
       and_10_out, and_11_out, and_12_out, and_13_out, Clock_out, nor_1_out, nor_2_out, nor_3_out, nor_4_out,
       nor_5_out, nor_6_out, not_1_out, not_2_out, not_3_out, not_4_out, not_5_out, not_6_out, not_7_out;

  not not_1 (not_1_out, S0);
  not not_2 (not_2_out, S1);
  Clock Clock (.out(Clock_out));
  nor nor_1 (nor_1_out, not_1_out, not_2_out);
  and and_1 (and_1_out, not_2_out, not_1_out);
  not not_3 (not_3_out, Clock_out);
  and and_2 (and_2_out, right_serial, not_2_out);
  nor nor_2 (nor_2_out, and_1_out, not_3_out);
  and and_3 (and_3_out, nor_1_out, A);
  nor nor_3 (nor_3_out, and_2_out, and_3_out, and_4_out);
  and and_4 (and_4_out, not_1_out, QB);
  not not_4 (not_4_out, nor_3_out);
  and and_5 (and_5_out, nor_1_out, B);
  and and_6 (and_6_out, QA, not_2_out);
  D_Flip_Flop #(.trigger("high")) d_ff_1 (
    .clk(nor_2_out), .D(not_4_out), .Q(QA), .reset(clear));  // open: Qn, preset, en
  and and_7 (and_7_out, not_1_out, QC);
  nor nor_4 (nor_4_out, and_6_out, and_5_out, and_7_out);
  and and_8 (and_8_out, QB, not_2_out);
  not not_5 (not_5_out, nor_4_out);
  and and_9 (and_9_out, nor_1_out, C);
  nor nor_5 (nor_5_out, and_8_out, and_9_out, and_10_out);
  D_Flip_Flop #(.trigger("high")) d_ff_2 (
    .clk(nor_2_out), .D(not_5_out), .Q(QB), .reset(clear));  // open: Qn, preset, en
  and and_10 (and_10_out, not_1_out, QD);
  not not_6 (not_6_out, nor_5_out);
  and and_11 (and_11_out, QC, not_2_out);
  and and_12 (and_12_out, nor_1_out, D);
  nor nor_6 (nor_6_out, and_11_out, and_12_out, and_13_out);
  D_Flip_Flop #(.trigger("high")) d_ff_3 (
    .clk(nor_2_out), .D(not_6_out), .Q(QC), .reset(clear));  // open: Qn, preset, en
  and and_13 (and_13_out, not_1_out, left_serial);
  not not_7 (not_7_out, nor_6_out);
  D_Flip_Flop #(.trigger("high")) d_ff_4 (
    .clk(nor_2_out), .D(not_7_out), .Q(QD), .reset(clear));  // open: Qn, preset, en
endmodule
