// Logisim project Sec_A1_Group_2_Problem_1.circ as structural Verilog: 1 circuit, main circuit main
module main (
  input  J,
  input  K,
  output Q,
  output Q_prime
);

  wire Clock_out, n7400_1_p3, n7400_1_p4, n7400_1_p6, n7400_1_p11, n7400_1_p12, n7400_1_p14, n7400_3_p2,
       n7400_3_p3, n7400_3_p10, n7400_3_p13, n7400_4_p3;

  Clock Clock (.out(Clock_out));
  // _7400 7400_1: pin names not known; wires that end beside it: Q_prime, Clock_out, n7400_1_p3, n7400_1_p4, J, n7400_1_p6, 1'b0, 1'b1, Clock_out, Q, n7400_1_p11, n7400_1_p12, K, n7400_1_p14
  // _7400 7400_2: pin names not known; wires that end beside it: n7400_1_p3, n7400_1_p3, n7400_1_p4, 1'b0, 1'b1, n7400_1_p12, 1'b0
  // _7400 7400_3: pin names not known; wires that end beside it: n7400_1_p6, n7400_3_p2, n7400_3_p3, n7400_3_p3, n7400_1_p14, n7400_3_p2, 1'b1, Clock_out, Clock_out, n7400_3_p10, n7400_3_p3, n7400_3_p10, n7400_3_p13
  // _7400 7400_4: pin names not known; wires that end beside it: n7400_3_p10, n7400_3_p2, n7400_4_p3, n7400_4_p3, Q, Q_prime, 1'b0, 1'b1, n7400_3_p13, Q_prime, Q
endmodule
