// Logisim project Sec_A1_Group_2_Problem_2.circ as structural Verilog: 1 circuit, main circuit main
// QA
module main (
  input  RSSIn,
  input  A,
  input  B,
  input  C,
  input  D,
  input  LSSIn,
  input  S0,
  input  S1,
  input  Clear,
  output QA,
  output QB,
  output QC,
  output QD
);

  wire clock_1_out, n7402_1_p4, n7404_1_p2, n7404_1_p4, n7404_1_p5, n7404_1_p6, n7404_1_p9, n7404_1_p10,
       n7404_1_p11, n7404_1_p12, n7404_1_p13, n7404_1_p14, n7408_1_p3, n7408_2_p2, n7408_2_p3, n7408_2_p6,
       n7408_2_p11, n7408_2_p14, n7408_3_p11, n7408_3_p14, n7427_1_p1, n7427_1_p3, n7427_1_p5, n7427_1_p9,
       n7427_2_p3, n7427_2_p9;

  Clock clock_1 (.out(clock_1_out));
  // _7404 7404_1: pin names not known; wires that end beside it: S0, n7404_1_p2, S1, n7404_1_p4, n7404_1_p5, n7404_1_p6, 1'b0, 1'b1, n7404_1_p9, n7404_1_p10, n7404_1_p11, n7404_1_p12, n7404_1_p13, n7404_1_p14
  // _7408 7408_1: pin names not known; wires that end beside it: n7404_1_p4, n7404_1_p2, n7408_1_p3, 1'b0, 1'b1
  // _7408 7408_2: pin names not known; wires that end beside it: A, n7408_2_p2, n7408_2_p3, B, n7408_2_p2, n7408_2_p6, 1'b0, 1'b1, C, n7408_2_p2, n7408_2_p11, D, n7408_2_p2, n7408_2_p14
  // _7402 7402_1: pin names not known; wires that end beside it: n7408_2_p2, n7404_1_p2, n7404_1_p4, n7402_1_p4, n7408_1_p3, clock_1_out, 1'b0, 1'b1
  // _7427 7427_1: pin names not known; wires that end beside it: n7427_1_p1, n7408_2_p3, n7427_1_p3, n7408_2_p6, n7427_1_p5, n7404_1_p9, 1'b0, 1'b1, n7427_1_p9, n7404_1_p5
  // _7474 7474_1: pin names not known; wires that end beside it: Clear, n7404_1_p6, n7402_1_p4, QA, 1'b0, 1'b1, Clear, n7404_1_p10, n7402_1_p4, QB
  // _7408 7408_3: pin names not known; wires that end beside it: n7404_1_p4, RSSIn, n7427_1_p1, n7404_1_p4, QA, n7427_1_p3, 1'b0, 1'b1, n7404_1_p4, QB, n7408_3_p11, n7404_1_p4, QC, n7408_3_p14
  // _7474 7474_2: pin names not known; wires that end beside it: Clear, n7404_1_p12, n7402_1_p4, QC, 1'b0, 1'b1, Clear, n7404_1_p14, n7402_1_p4, QD
  // _7427 7427_2: pin names not known; wires that end beside it: n7408_3_p11, n7408_2_p11, n7427_2_p3, n7404_1_p11, 1'b0, 1'b1, n7408_3_p14, n7408_2_p14, n7427_2_p9, n7404_1_p13
  // _7408 7408_4: pin names not known; wires that end beside it: n7404_1_p2, QB, n7427_1_p9, n7404_1_p2, QC, n7427_1_p5, 1'b0, 1'b1, n7404_1_p2, QD, n7427_2_p3, n7404_1_p2, LSSIn, n7427_2_p9
endmodule
