// Logisim project Group_2_Problem_2.circ as structural Verilog: 2 circuits, main circuit problem-2
module problem_2 (
  input  A,
  input  B,
  input  C,
  output out_4,
  output out_5,
  output out_6
);

  wire n7404_1_p4, n7404_1_p6, n7404_1_p8, n7408_1_p3, n7408_1_p6, n7408_1_p11, n7408_1_p14, n7408_2_p3,
       n7408_2_p6, n7408_2_p11, n7408_2_p14, n7408_3_p3, n7408_3_p6, n7432_1_p6, n7432_1_p11;

  // _7404 7404_1: pin names not known; wires that end beside it: 1'b0, 1'b1, A, n7404_1_p4, B, n7404_1_p6, C, n7404_1_p8
  // _7408 7408_1: pin names not known; wires that end beside it: A, n7404_1_p6, n7408_1_p3, n7404_1_p4, B, n7408_1_p6, 1'b0, 1'b1, n7404_1_p4, n7404_1_p6, n7408_1_p11, n7408_1_p11, C, n7408_1_p14
  // _7408 7408_2: pin names not known; wires that end beside it: n7404_1_p4, B, n7408_2_p3, n7408_2_p3, n7404_1_p8, n7408_2_p6, 1'b0, 1'b1, A, B, n7408_2_p11, n7408_2_p11, C, n7408_2_p14
  // _7408 7408_3: pin names not known; wires that end beside it: A, n7404_1_p6, n7408_3_p3, n7408_3_p3, n7404_1_p8, n7408_3_p6, 1'b0, 1'b1
  // _7432 7432_1: pin names not known; wires that end beside it: n7408_1_p6, n7408_1_p3, out_5, n7408_1_p14, n7408_2_p6, n7432_1_p6, 1'b0, 1'b1, n7408_2_p14, n7408_3_p6, n7432_1_p11, n7432_1_p11, n7432_1_p6, out_6

  assign out_4 = A;
endmodule

module problem_2_diagram (
  input  A,
  input  B,
  input  C,
  output X___A,
  output Y___AB_prime___A_prime_B,
  output Z___A_prime_B_prime_C___A_prime_BC_prime___ABC___AB_prime_C_prime
);

  wire and_1_out, and_2_out, and_3_out, and_4_out, and_5_out, and_6_out, and_7_out, and_8_out, and_9_out,
       and_10_out, not_1_out, not_2_out, not_3_out, or_2_out, or_3_out;

  not not_1 (not_1_out, A);
  not not_2 (not_2_out, B);
  not not_3 (not_3_out, C);
  and and_1 (and_1_out, A, not_2_out);
  and and_2 (and_2_out, not_1_out, B);
  or or_1 (Y___AB_prime___A_prime_B, and_1_out, and_2_out);
  and and_3 (and_3_out, not_1_out, not_2_out);
  and and_4 (and_4_out, and_3_out, C);
  and and_5 (and_5_out, not_1_out, B);
  and and_6 (and_6_out, and_5_out, not_3_out);
  and and_7 (and_7_out, A, B);
  and and_8 (and_8_out, and_7_out, C);
  and and_9 (and_9_out, A, not_2_out);
  and and_10 (and_10_out, and_9_out, not_3_out);
  or or_2 (or_2_out, and_4_out, and_6_out);
  or or_3 (or_3_out, and_8_out, and_10_out);
  or or_4 (Z___A_prime_B_prime_C___A_prime_BC_prime___ABC___AB_prime_C_prime, or_2_out, or_3_out);

  assign X___A = A;
endmodule
