// Logisim project Group_2_Problem_3.circ as structural Verilog: 2 circuits, main circuit main
module main (
  input  A,
  input  B,
  input  C,
  output LED1,
  output LED0
);

  wire n7404_1_p6, n7408_1_p3, n7408_1_p6, n7408_1_p9, n7408_1_p10, n7408_1_p11, n7408_1_p14, n7408_2_p6,
       n7408_2_p11, n7408_3_p6, n7432_1_p3, n7432_1_p9, n7432_1_p10, n7432_1_p11, n7432_1_p12, n7432_1_p13,
       n7432_2_p2;

  // _7408 7408_1: pin names not known; wires that end beside it: A, B, n7408_1_p3, B, C, n7408_1_p6, 1'b0, 1'b1, n7408_1_p9, n7408_1_p10, n7408_1_p11, C, A, n7408_1_p14
  // _7404 7404_1: pin names not known; wires that end beside it: A, n7408_1_p9, B, n7408_1_p10, C, n7404_1_p6, 1'b0, 1'b1
  // _7432 7432_1: pin names not known; wires that end beside it: n7408_1_p3, n7408_1_p6, n7432_1_p3, n7432_1_p3, n7408_1_p14, LED1, 1'b0, 1'b1, n7432_1_p9, n7432_1_p10, n7432_1_p11, n7432_1_p12, n7432_1_p13, n7432_1_p9
  // _7408 7408_2: pin names not known; wires that end beside it: n7408_1_p11, C, n7432_1_p12, B, n7408_1_p9, n7408_2_p6, 1'b0, 1'b1, A, n7408_1_p10, n7408_2_p11, n7404_1_p6, n7408_2_p6, n7432_1_p13
  // _7432 7432_2: pin names not known; wires that end beside it: n7432_1_p11, n7432_2_p2, LED0, 1'b0, 1'b1
  // _7408 7408_3: pin names not known; wires that end beside it: n7408_2_p11, n7404_1_p6, n7432_1_p10, A, B, n7408_3_p6, 1'b0, 1'b1, C, n7408_3_p6, n7432_2_p2
endmodule

module gate_circ (
  input  A,
  input  B,
  input  C,
  output LED1,
  output LED0
);

  wire and_1_out, and_2_out, and_3_out, and_4_out, and_5_out, and_6_out, and_7_out, and_8_out, and_9_out,
       and_10_out, and_11_out, not_1_out, not_2_out, not_3_out, not_4_out, not_5_out, not_6_out, or_1_out,
       or_3_out, or_4_out;

  and and_1 (and_1_out, B, C);
  and and_2 (and_2_out, A, C);
  not not_1 (not_1_out, A);
  not not_2 (not_2_out, B);
  not not_3 (not_3_out, A);
  not not_4 (not_4_out, B);
  or or_1 (or_1_out, and_1_out, and_2_out);
  and and_3 (and_3_out, A, B);
  and and_4 (and_4_out, not_1_out, not_2_out);
  and and_5 (and_5_out, not_3_out, B);
  not not_5 (not_5_out, C);
  and and_6 (and_6_out, A, not_4_out);
  not not_6 (not_6_out, C);
  and and_7 (and_7_out, A, B);
  or or_2 (LED1, or_1_out, and_3_out);
  and and_8 (and_8_out, and_4_out, C);
  and and_9 (and_9_out, and_5_out, not_5_out);
  and and_10 (and_10_out, and_6_out, not_6_out);
  and and_11 (and_11_out, and_7_out, C);
  or or_3 (or_3_out, and_8_out, and_9_out);
  or or_4 (or_4_out, and_10_out, and_11_out);
  or or_5 (LED0, or_3_out, or_4_out);
endmodule
