// Logisim project Group_2_Problem_4.circ as structural Verilog: 2 circuits, main circuit Problem4
module Problem4 (
  input  A,
  input  B,
  input  C,
  input  D,
  output F
);

  wire n7404_1_p2, n7404_1_p4, n7404_1_p8, n7404_1_p10, n7408_1_p3, n7408_1_p6, n7408_1_p11, n7408_1_p14,
       n7408_2_p3, n7408_2_p11, n7408_2_p14, n7408_3_p3, n7408_3_p6, n7432_1_p1, n7432_1_p2, n7432_1_p7,
       n7432_1_p8, n7432_1_p10;

  // _7404 7404_1: pin names not known; wires that end beside it: A, n7404_1_p2, D, n7404_1_p4, 1'b0, 1'b1, B, n7404_1_p8, C, n7404_1_p10
  // _7408 7408_1: pin names not known; wires that end beside it: n7404_1_p2, B, n7408_1_p3, n7408_1_p3, C, n7408_1_p6, 1'b0, 1'b1, n7408_1_p6, n7404_1_p4, n7408_1_p11, A, D, n7408_1_p14
  // _7432 7432_1: pin names not known; wires that end beside it: n7432_1_p1, n7432_1_p2, F, 1'b0, 1'b1, n7408_1_p11, n7432_1_p7, n7432_1_p8, n7432_1_p8, n7432_1_p10, n7432_1_p1
  // _7408 7408_2: pin names not known; wires that end beside it: n7408_1_p14, n7404_1_p8, n7408_2_p3, n7408_2_p3, n7404_1_p10, n7432_1_p7, 1'b0, 1'b1, A, B, n7408_2_p11, n7408_2_p11, n7404_1_p10, n7408_2_p14
  // _7408 7408_3: pin names not known; wires that end beside it: A, B, n7408_3_p3, n7408_3_p3, C, n7408_3_p6, 1'b0, 1'b1, n7408_2_p14, n7404_1_p4, n7432_1_p10, n7408_3_p6, D, n7432_1_p2
endmodule

module Circuit_Diagram (
  input  A,
  input  B,
  input  C,
  input  D,
  output F
);

  wire and_1_out, and_2_out, and_3_out, and_4_out, and_5_out, and_6_out, and_7_out, and_8_out, and_9_out,
       and_10_out, and_11_out, and_12_out, not_1_out, not_2_out, not_3_out, not_4_out, not_5_out, not_6_out,
       or_1_out, or_2_out;

  not not_1 (not_1_out, A);
  and and_1 (and_1_out, not_1_out, B);
  and and_2 (and_2_out, C, not_2_out);
  not not_2 (not_2_out, D);
  and and_3 (and_3_out, A, not_3_out);
  not not_3 (not_3_out, B);
  not not_4 (not_4_out, C);
  and and_4 (and_4_out, not_4_out, D);
  and and_5 (and_5_out, A, B);
  not not_5 (not_5_out, C);
  and and_6 (and_6_out, not_5_out, not_6_out);
  not not_6 (not_6_out, D);
  and and_7 (and_7_out, A, B);
  and and_8 (and_8_out, C, D);
  and and_9 (and_9_out, and_1_out, and_2_out);
  and and_10 (and_10_out, and_3_out, and_4_out);
  and and_11 (and_11_out, and_5_out, and_6_out);
  and and_12 (and_12_out, and_7_out, and_8_out);
  or or_1 (or_1_out, and_9_out, and_10_out);
  or or_2 (or_2_out, and_11_out, and_12_out);
  or or_3 (F, or_1_out, or_2_out);
endmodule
