// Logisim project 1805006.circ as structural Verilog: 1 circuit, main circuit main
module main (
  output out_1,
  output out_2,
  output out_3,
  output out_4
);

  wire clock_1_out, n7408_1_p3, n7408_1_p6, n7408_1_p11, n7408_1_p14, n7408_2_p3, n7408_2_p11, n7408_3_p3,
       n7408_3_p6, n7432_1_p4, n7432_1_p10, n7432_1_p12, n7474_1_p1, n7474_1_p2, n7474_1_p8, n7474_2_p3,
       n7474_2_p6, n7474_2_p8, n7474_2_p11;

  Clock clock_1 (.out(clock_1_out));
  // _7474 7474_1: pin names not known; wires that end beside it: n7474_1_p1, n7474_1_p2, clock_1_out, out_4, n7474_1_p2, 1'b1, n7474_1_p1, n7474_1_p8, clock_1_out, out_3
  // _7474 7474_2: pin names not known; wires that end beside it: 1'b0, n7474_1_p1, n7474_2_p3, clock_1_out, out_2, n7474_2_p6, 1'b0, n7474_2_p8, 1'b1, n7474_1_p1, n7474_2_p11, clock_1_out, out_1
  // _7408 7408_1: pin names not known; wires that end beside it: out_3, n7474_1_p2, n7408_1_p3, n7474_2_p8, out_4, n7408_1_p6, 1'b0, 1'b1, out_2, n7474_2_p8, n7408_1_p11, out_2, n7474_1_p2, n7408_1_p14
  // _7432 7432_1: pin names not known; wires that end beside it: n7408_1_p3, n7408_1_p6, n7474_1_p8, n7432_1_p4, out_1, n7474_2_p11, 1'b1, n7408_1_p11, n7408_1_p14, n7432_1_p10, n7432_1_p10, n7432_1_p12, n7474_2_p3
  // _7408 7408_2: pin names not known; wires that end beside it: n7474_2_p6, out_4, n7408_2_p3, n7408_2_p3, out_3, n7432_1_p12, 1'b0, 1'b1, out_4, out_3, n7408_2_p11, n7408_2_p11, out_2, n7432_1_p4
  // _7408 7408_3: pin names not known; wires that end beside it: n7474_1_p2, n7474_2_p8, n7408_3_p3, n7408_3_p3, out_2, n7408_3_p6, 1'b0, 1'b1, n7408_3_p6, out_1, n7474_1_p1
endmodule
