// Logisim project 1805006.circ as structural Verilog: 1 circuit, main circuit main
module main (
  output Y2,
  output Y1,
  output Y0
);

  wire clock_1_out, n7408_1_p3, n7474_1_p4;

  Clock clock_1 (.out(clock_1_out));
  // _7474 7474_1: pin names not known; wires that end beside it: Y1, clock_1_out, Y0, n7474_1_p4, 1'b0, 1'b1, n7474_1_p4, clock_1_out, Y1
  // _7408 7408_1: pin names not known; wires that end beside it: Y1, Y0, n7408_1_p3, 1'b0, 1'b1
  // _7474 7474_2: pin names not known; wires that end beside it: n7408_1_p3, clock_1_out, Y2, 1'b0, 1'b1
endmodule
