// Logisim project 1805006.circ as structural Verilog: 1 circuit, main circuit main
module main (
  input  P,
  input  Q,
  input  R,
  input  S,
  output out_5
);

  wire n7404_1_p2, n7404_1_p4, n7408_1_p3, n7408_1_p6, n7408_1_p9, n7432_1_p3;

  // _7404 7404_1: pin names not known; wires that end beside it: P, n7404_1_p2, Q, n7404_1_p4
  // _7408 7408_1: pin names not known; wires that end beside it: n7404_1_p2, n7404_1_p4, n7408_1_p3, n7404_1_p2, S, n7408_1_p6, S, R, n7408_1_p9
  // _7432 7432_1: pin names not known; wires that end beside it: n7408_1_p3, n7408_1_p6, n7432_1_p3, n7432_1_p3, n7408_1_p9, out_5
endmodule
