// Logisim project 1805006.circ as structural Verilog: 1 circuit, main circuit main
module main (
  input  Constants,
  input  A,
  input  B,
  input  C,
  input  D,
  output out_6
);

  wire n7404_1_p2, n7404_1_p6, n74153_1_p7, n74153_1_p16;

  // _7404 7404_1: pin names not known; wires that end beside it: D, n7404_1_p2, 1'b0, 1'b1, Constants, n7404_1_p6
  // _74153 74153_1: pin names not known; wires that end beside it: Constants, B, n7404_1_p2, Constants, n7404_1_p6, Constants, n74153_1_p7, 1'b0, 1'b1, Constants, C, Constants, D, D, D, n74153_1_p16
  // _74157 74157_1: pin names not known; wires that end beside it: A, n74153_1_p7, n74153_1_p16, out_6, 1'b0, 1'b1, Constants
endmodule
