// Logisim project Group_A1_2_Problem_1.circ as structural Verilog: 1 circuit, main circuit main
module main (
  input  A1,
  input  A0,
  input  B1,
  input  B0,
  output L,
  output E,
  output G
);

  wire n7404_1_p2, n7404_1_p4, n7404_1_p5, n7404_1_p6, n7404_1_p10, n7404_1_p12, n7404_1_p13, n7404_1_p14,
       n7408_1_p4, n7408_1_p7, n7408_1_p12, n7408_1_p15, n7408_2_p3, n7408_2_p6;

  // _7404 7404_1: pin names not known; wires that end beside it: A1, n7404_1_p2, A0, n7404_1_p4, n7404_1_p5, n7404_1_p6, 1'b0, 1'b1, B0, n7404_1_p10, B1, n7404_1_p12, n7404_1_p13, n7404_1_p14
  // _7486 7486_1: pin names not known; wires that end beside it: A1, B1, n7404_1_p5, 1'b1, A0, B0, n7404_1_p13
  // _7408 7408_1: pin names not known; wires that end beside it: 1'b0, n7404_1_p2, B1, n7408_1_p4, n7404_1_p6, n7404_1_p4, n7408_1_p7, 1'b0, 1'b1, n7404_1_p10, A0, n7408_1_p12, B0, n7408_1_p7, n7408_1_p15
  // _7408 7408_2: pin names not known; wires that end beside it: n7404_1_p6, n7408_1_p12, n7408_2_p3, A1, n7404_1_p12, n7408_2_p6, 1'b0, 1'b1, n7404_1_p14, n7404_1_p6, E
  // _7432 7432_1: pin names not known; wires that end beside it: n7408_1_p4, n7408_1_p15, L, n7408_2_p3, n7408_2_p6, G, 1'b0, 1'b1
endmodule
