// Logisim project Group_A1_2_Problem_2.circ as structural Verilog: 2 circuits, main circuit main
module main (
  input  P,
  input  Q,
  input  R,
  output D,
  output B
);

  wire AND_p3, AND_p6, AND_p10, NOT_p2, OR_p3, XOR_p3;

  // _7404 NOT: pin names not known; wires that end beside it: P, NOT_p2, 1'b0, 1'b1
  // _7408 AND: pin names not known; wires that end beside it: NOT_p2, R, AND_p3, NOT_p2, Q, AND_p6, 1'b1, R, Q, AND_p10
  // _7432 OR: pin names not known; wires that end beside it: AND_p3, AND_p6, OR_p3, OR_p3, AND_p10, B, 1'b0, 1'b0, 1'b1
  // _7486 XOR: pin names not known; wires that end beside it: P, Q, XOR_p3, XOR_p3, R, D, 1'b0, 1'b1
endmodule

module Circuit_Diagram (
  input  P,
  input  Q,
  input  R,
  output D,
  output B
);

  wire and_1_out, and_2_out, and_3_out, not_1_out, or_1_out, xor_1_out;

  not not_1 (not_1_out, P);
  xor xor_1 (xor_1_out, P, Q);
  and and_1 (and_1_out, not_1_out, R);
  and and_2 (and_2_out, not_1_out, Q);
  and and_3 (and_3_out, R, Q);
  xor xor_2 (D, xor_1_out, R);
  or or_1 (or_1_out, and_1_out, and_2_out);
  or or_2 (B, or_1_out, and_3_out);
endmodule
