// Logisim project 1805006.circ as structural Verilog: 1 circuit, main circuit main
module main (
  input  X1,
  input  X2,
  input  En,
  output Z
);

  wire n7404_1_p2, n7404_1_p4, n7404_1_p5, n7404_1_p6, n7404_1_p7, n7404_1_p8, n7404_1_p9, n7404_1_p10;

  // _7404 7404_1: pin names not known; wires that end beside it: X1, n7404_1_p2, X2, n7404_1_p4, n7404_1_p5, n7404_1_p6, n7404_1_p7, n7404_1_p8, n7404_1_p9, n7404_1_p10
  // _7408 7408_1: pin names not known
  // _7408 7408_2: pin names not known
  // _7408 7408_3: pin names not known
  // _74116 74116_1: pin names not known; wires that end beside it: En, En, n7404_1_p5, n7404_1_p7, n7404_1_p9
  // _7432 7432_1: pin names not known
  // _7432 7432_2: pin names not known; wires that end beside it: Z
endmodule
